# Fritzing sketch led-switch-toggle (saved by Fritzing 0.9.2b)
breadboards: 1

parts:
  Pi1 = Adafruit Pi Cobbler
  LED1 = LED - 5mm [color="Red (635nm)" package="5 mm [THT]"]
  S1 = Pushbutton [package="[THT]"]

nets:
  N1: Pi1.#24, S1.Pin_1, S1.Pin_2
  N2: Pi1.#25, LED1.anode
  N3: Pi1.PIN25, S1.Pin_3, S1.Pin_4

notes:
  Switch is set so when pressed, the input received through pin 18 is HIGH, so it triggers the LED pin to set to HIGH.

custom parts:
  Adafruit Pi Cobbler: Adafruit Pi Cobbler GPIO Breakout for Raspberry Pi
